# Fritzing sketch HC-05 Accel Wiring (saved by Fritzing 0.9.3b)
breadboards: 1

parts:
  Part1 = Arduino Uno (Rev3)
  GY1 = MPU-6050 Board GY-521 [form="♀ (female)" package=THT]
  HC-05 = Bluetooth HC-05 Macho
  R1 = PHOTOCELL [package=photocell-kit]
  R2 = Resistor [tolerance=±5% resistance=10k package=THT]

nets:
  N1: Part1.A0, R1.P$2, R2.Pin_0
  N2: Part1.A4/SDA, GY1.pin4
  N3: Part1.A5/SCL, GY1.pin3
  N4: Part1.D10_PWM/SS, HC-05.TXD
  N5: Part1.D11_PWM/MOSI, HC-05.RXD
  N6: Part1.D2, GY1.pin8
  5V: Part1.5V, GY1.pin1, HC-05.VCC, R1.P$1
  GND: Part1.GND, GY1.pin2, GY1.pin7, HC-05.GND, R2.Pin_1

custom parts:
  MPU-6050 Board GY-521: Acelerometro y Giroscopio MPU-6050 Board GY-521
